// Logisim project counter.circ as structural Verilog: 8 circuits, main circuit RS
module RS (
  input  S,
  input  C,
  input  R,
  input  RESET,
  output nQ,
  output Q
);

  wire and_1_out, and_2_out, not_1_out, not_2_out, not_3_out, or_1_out, or_2_out, or_3_out, por_1_out;

  and and_1 (and_1_out, S, C);
  and and_2 (and_2_out, C, R);
  not not_1 (not_1_out, RESET);
  POR por_1 (.out(por_1_out));
  or or_1 (or_1_out, RESET, not_2_out);
  not not_2 (not_2_out, or_2_out);
  or or_2 (or_2_out, and_1_out, Q);
  or or_3 (or_3_out, nQ, and_2_out);
  not not_3 (not_3_out, or_3_out);
  and and_3 (Q, not_3_out, not_1_out);
  or or_4 (nQ, por_1_out, or_1_out);
endmodule

module TT (
  input  D,
  input  C,
  input  RESET,
  output Q1,
  output Q
);

  wire not_1_out, t_1_q;

  not not_1 (not_1_out, C);
  T t_1 (.D(D), .C(not_1_out), .RESET(RESET), .Q(t_1_q));  // open: Q1
  T t_2 (.D(t_1_q), .C(C), .RESET(RESET), .Q1(Q1), .Q(Q));
endmodule

module T (
  input  D,
  input  C,
  input  RESET,
  output Q1,
  output Q
);

  wire not_1_out;

  not not_1 (not_1_out, D);
  RS rs_1 (.S(D), .C(C), .R(not_1_out), .RESET(RESET), .nQ(Q1), .Q(Q));
endmodule

module DF (
  input  C,
  input  RESET,
  output Q
);

  wire tt_1_q1;

  TT tt_1 (.D(tt_1_q1), .C(C), .RESET(RESET), .Q1(tt_1_q1), .Q(Q));
endmodule

module cnt (
  input  C,
  output out_2,
  output out_3,
  output out_4,
  output out_5,
  output out_6,
  output out_7,
  output out_8,
  output out_9,
  output out_10,
  output out_11,
  output out_12,
  output out_13,
  output out_14,
  output out_15,
  output out_16,
  output out_17,
  output out_18
);

  wire and_1_out, df_1_q, df_2_q, df_3_q, df_4_q, df_5_q, df_6_q, undriven;

  DF df_1 (.C(C), .RESET(and_1_out), .Q(df_1_q));
  DF df_2 (.C(df_1_q), .RESET(and_1_out), .Q(df_2_q));
  DF df_3 (.C(df_2_q), .RESET(and_1_out), .Q(df_3_q));
  DF df_4 (.C(df_3_q), .RESET(and_1_out), .Q(df_4_q));
  five five_1 (
    .X1(df_1_q), .X2(df_2_q), .X3(df_3_q), .X4(df_4_q), .X5(df_5_q), .a0(out_2), .a1(out_3), .a2(out_4),
    .a3(out_5), .a4(out_6), .a5(out_7), .a6(out_8), .a7(out_9), .a8(out_10), .a9(out_11), .a10(out_12),
    .a11(out_13), .a12(out_14), .a13(out_15), .a14(out_16), .a15(out_17), .a16(out_18));
  DF df_5 (.C(df_4_q), .RESET(undriven), .Q(df_5_q));
  DF df_6 (.C(df_5_q), .RESET(and_1_out), .Q(df_6_q));
  and and_1 (and_1_out, df_1_q, df_6_q, df_4_q, df_2_q, df_5_q, df_3_q);
endmodule

module Two (
  input  X1,
  input  X2,
  input  C,
  output a0,
  output a1,
  output a2,
  output a3
);

  wire not_1_out, not_2_out, not_3_out, not_4_out;

  not not_1 (not_1_out, X1);
  not not_2 (not_2_out, X2);
  not not_3 (not_3_out, X2);
  not not_4 (not_4_out, X1);
  and and_1 (a0, not_1_out, C, not_2_out);
  and and_2 (a1, X1, C, not_3_out);
  and and_3 (a2, not_4_out, C, X2);
  and and_4 (a3, X1, C, X2);
endmodule

module three (
  input  X1,
  input  X2,
  input  X3,
  input  C,
  output a0,
  output a1,
  output a2,
  output a3,
  output a4,
  output a5,
  output a6,
  output a7
);

  wire and_1_out, and_2_out, not_1_out;

  not not_1 (not_1_out, X3);
  and and_1 (and_1_out, X3, C);
  and and_2 (and_2_out, not_1_out, C);
  Two two_1 (.X1(X1), .X2(X2), .C(and_2_out), .a0(a0), .a1(a1), .a2(a2), .a3(a3));
  Two two_2 (.X1(X1), .X2(X2), .C(and_1_out), .a0(a4), .a1(a5), .a2(a6), .a3(a7));
endmodule

module five (
  input  X1,
  input  X2,
  input  X3,
  input  X4,
  input  X5,
  output a0,
  output a1,
  output a2,
  output a3,
  output a4,
  output a5,
  output a6,
  output a7,
  output a8,
  output a9,
  output a10,
  output a11,
  output a12,
  output a13,
  output a14,
  output a15,
  output a16
);

  wire and_1_out, and_2_out, not_1_out, not_2_out;

  not not_1 (not_1_out, X4);
  not not_2 (not_2_out, X5);
  and and_1 (and_1_out, not_1_out, not_2_out);
  and and_2 (and_2_out, X4, not_2_out);
  three three_1 (
    .X1(X1), .X2(X2), .X3(X3), .C(and_1_out), .a0(a0), .a1(a1), .a2(a2), .a3(a3), .a4(a4), .a5(a5), .a6(a6),
    .a7(a7));
  three three_2 (
    .X1(X1), .X2(X2), .X3(X3), .C(and_2_out), .a0(a8), .a1(a9), .a2(a10), .a3(a11), .a4(a12), .a5(a13),
    .a6(a14), .a7(a15));

  assign a16 = X5;
endmodule
