// Logisim project lfsr.circ as structural Verilog: 4 circuits, main circuit lfsr
module RS (
  input  S,
  input  C,
  input  R,
  input  RESET,
  output nQ,
  output Q
);

  wire and_1_out, and_2_out, not_1_out, not_2_out, not_3_out, or_1_out, or_2_out, or_3_out, por_1_out;

  and and_1 (and_1_out, S, C);
  and and_2 (and_2_out, C, R);
  not not_1 (not_1_out, or_2_out);
  not not_2 (not_2_out, RESET);
  POR por_1 (.out(por_1_out));
  or or_1 (or_1_out, RESET, not_1_out);
  or or_2 (or_2_out, and_1_out, Q);
  or or_3 (or_3_out, nQ, and_2_out);
  not not_3 (not_3_out, or_3_out);
  and and_3 (Q, not_3_out, not_2_out);
  or or_4 (nQ, por_1_out, or_1_out);
endmodule

module TT (
  input  D,
  input  C,
  input  RESET,
  output Q1,
  output Q
);

  wire not_1_out, t_1_q;

  not not_1 (not_1_out, C);
  T t_1 (.D(D), .C(not_1_out), .RESET(RESET), .Q(t_1_q));  // open: Q1
  T t_2 (.D(t_1_q), .C(C), .RESET(RESET), .Q1(Q1), .Q(Q));
endmodule

module T (
  input  D,
  input  C,
  input  RESET,
  output Q1,
  output Q
);

  wire not_1_out;

  not not_1 (not_1_out, D);
  RS rs_1 (.S(D), .C(C), .R(not_1_out), .RESET(RESET), .nQ(Q1), .Q(Q));
endmodule

module lfsr (
  input  d5,
  input  d0,
  input  d1,
  input  d2,
  input  d3,
  input  d4,
  input  in_7,
  output x6,
  output x5,
  output x4,
  output x3,
  output x2,
  output x1
);

  wire or_1_out, or_2_out, or_3_out, or_4_out, or_5_out, or_6_out, xor_1_out;

  xor xor_1 (xor_1_out, or_6_out, x1);
  TT tt_1 (.D(xor_1_out), .C(in_7), .Q(x1));  // open: RESET, Q1
  or or_1 (or_1_out, d0, x1);
  TT tt_2 (.D(or_1_out), .C(in_7), .Q(x2));  // open: RESET, Q1
  or or_2 (or_2_out, d1, x2);
  or or_3 (or_3_out, d2, x3);
  TT tt_3 (.D(or_2_out), .C(in_7), .Q(x3));  // open: RESET, Q1
  TT tt_4 (.D(or_3_out), .C(in_7), .Q(x4));  // open: RESET, Q1
  or or_4 (or_4_out, d3, x4);
  or or_5 (or_5_out, d4, x5);
  TT tt_5 (.D(or_4_out), .C(in_7), .Q(x5));  // open: RESET, Q1
  or or_6 (or_6_out, d5, x6);
  TT tt_6 (.D(or_5_out), .C(in_7), .Q(x6));  // open: RESET, Q1
endmodule
